// Logisim project ALU.circ as structural Verilog: 7 circuits, main circuit main
module main (
  input  in_1,
  input  in_2,
  input  in_3,
  input  in_4,
  input  in_5,
  input  in_6,
  input  in_7,
  input  in_8,
  input  in_9,
  input  in_10,
  input  in_11,
  input  in_12,
  input  in_13,
  input  in_14,
  input  in_15,
  input  in_16,
  input  in_17,
  input  in_18,
  output out_19,
  output out_20,
  output out_21,
  output out_22,
  output out_23,
  output out_24,
  output out_25,
  output out_26
);

  _8_Bit_Adder Adder ();  // open: in_1, in_2, in_3, out_4, out_5
  _8_Bit_Subtractor Subtractor ();  // open: in_1, in_2, in_3, in_4, in_5, in_6, in_7, in_8, in_9, in_10, in_11, in_12, in_13, in_14, in_15, in_16, out_17, out_18, out_19, out_20, out_21, out_22, out_23, out_24
endmodule

module Half_Adder (
  input  in_1,
  input  in_2,
  output Sum,
  output Carry
);

  wire not_1_out, or_1_out;

  or or_1 (or_1_out, in_1, in_2);
  not not_1 (not_1_out, Carry);
  and and_1 (Carry, in_1, in_2);
  and and_2 (Sum, or_1_out, not_1_out);
endmodule

module Full_Adder (
  input  in_1,
  input  in_2,
  input  in_3,
  output out_4,
  output out_5
);

  wire half_adder_1_carry, half_adder_1_sum, half_adder_2_carry;

  Half_Adder half_adder_1 (.in_1(in_1), .in_2(in_2), .Sum(half_adder_1_sum), .Carry(half_adder_1_carry));
  Half_Adder half_adder_2 (.in_1(half_adder_1_sum), .in_2(in_3), .Sum(out_4), .Carry(half_adder_2_carry));
  or or_1 (out_5, half_adder_1_carry, half_adder_2_carry);
endmodule

module _8_Bit_Adder (
  input  in_1,
  input  [7:0] in_2,
  input  [7:0] in_3,
  output [7:0] out_4,
  output out_5
);

  wire full_adder_1_out_5, full_adder_2_out_5, full_adder_3_out_5, full_adder_4_out_5, full_adder_5_out_5,
       full_adder_6_out_5, full_adder_7_out_5;

  Full_Adder full_adder_1 (.in_1(in_1), .in_2(in_2[0]), .in_3(in_3[0]), .out_4(out_4[0]), .out_5(full_adder_1_out_5));
  Full_Adder full_adder_2 (
    .in_1(full_adder_1_out_5), .in_2(in_2[1]), .in_3(in_3[1]), .out_4(out_4[1]), .out_5(full_adder_2_out_5));
  Full_Adder full_adder_3 (
    .in_1(full_adder_2_out_5), .in_2(in_2[2]), .in_3(in_3[2]), .out_4(out_4[2]), .out_5(full_adder_3_out_5));
  Full_Adder full_adder_4 (
    .in_1(full_adder_3_out_5), .in_2(in_2[3]), .in_3(in_3[3]), .out_4(out_4[3]), .out_5(full_adder_4_out_5));
  Full_Adder full_adder_5 (
    .in_1(full_adder_4_out_5), .in_2(in_2[4]), .in_3(in_3[4]), .out_4(out_4[4]), .out_5(full_adder_5_out_5));
  Full_Adder full_adder_6 (
    .in_1(full_adder_5_out_5), .in_2(in_2[5]), .in_3(in_3[5]), .out_4(out_4[5]), .out_5(full_adder_6_out_5));
  Full_Adder full_adder_7 (
    .in_1(full_adder_6_out_5), .in_2(in_2[6]), .in_3(in_3[6]), .out_4(out_4[6]), .out_5(full_adder_7_out_5));
  Full_Adder full_adder_8 (.in_1(full_adder_7_out_5), .in_2(in_2[7]), .in_3(in_3[7]), .out_4(out_4[7]), .out_5(out_5));
endmodule

module _8_Bit_Subtractor (
  input  in_1,
  input  in_2,
  input  in_3,
  input  in_4,
  input  in_5,
  input  in_6,
  input  in_7,
  input  in_8,
  input  in_9,
  input  in_10,
  input  in_11,
  input  in_12,
  input  in_13,
  input  in_14,
  input  in_15,
  input  in_16,
  output out_17,
  output out_18,
  output out_19,
  output out_20,
  output out_21,
  output out_22,
  output out_23,
  output out_24
);

  wire not_1_out, not_2_out, not_3_out, not_4_out, not_5_out, not_6_out, not_7_out, not_8_out;

  not not_1 (not_1_out, in_9);
  not not_2 (not_2_out, in_10);
  not not_3 (not_3_out, in_11);
  not not_4 (not_4_out, in_12);
  not not_5 (not_5_out, in_13);
  not not_6 (not_6_out, in_14);
  not not_7 (not_7_out, in_15);
  not not_8 (not_8_out, in_16);
  // _8_Bit_Adder 8_bit_adder_1: pin names not known; wires that end beside it: in_1, in_2, in_3, in_4, in_5, in_6, in_7, in_8, not_1_out, out_17, out_18, out_19, out_20, out_21, out_22
endmodule

module _8_by_1_bit_Multiplier (
  input  in_1,
  input  [7:0] in_2,
  output [7:0] out_3
);

  and and_1 (out_3[0], in_2[0], in_1);
  and and_2 (out_3[1], in_2[1], in_1);
  and and_3 (out_3[2], in_2[2], in_1);
  and and_4 (out_3[3], in_2[3], in_1);
  and and_5 (out_3[4], in_2[4], in_1);
  and and_6 (out_3[5], in_2[5], in_1);
  and and_7 (out_3[6], in_2[6], in_1);
  and and_8 (out_3[7], in_2[7], in_1);
endmodule

module _8_Bit_Multiplier (
  input  [7:0] in_1,
  input  [7:0] in_2,
  output [7:0] out_3
);

  wire [7:0] n8_bit_adder_1_out_4, n8_bit_adder_2_out_4, n8_bit_adder_3_out_4, n8_bit_adder_4_out_4,
       n8_bit_adder_5_out_4, n8_bit_adder_6_out_4, n8_bit_adder_8_out_4, n8_by_1_bit_multiplier_1_out_3,
       n8_by_1_bit_multiplier_2_out_3, n8_by_1_bit_multiplier_3_out_3, n8_by_1_bit_multiplier_4_out_3,
       n8_by_1_bit_multiplier_5_out_3, n8_by_1_bit_multiplier_6_out_3, n8_by_1_bit_multiplier_7_out_3,
       n8_by_1_bit_multiplier_8_out_3;

  _8_by_1_bit_Multiplier u_8_by_1_bit_multiplier_1 (
    .in_1(in_2[0]), .in_2(in_1), .out_3(n8_by_1_bit_multiplier_1_out_3));
  _8_by_1_bit_Multiplier u_8_by_1_bit_multiplier_2 (
    .in_1(in_2[1]), .in_2(in_1), .out_3(n8_by_1_bit_multiplier_2_out_3));
  _8_by_1_bit_Multiplier u_8_by_1_bit_multiplier_3 (
    .in_1(in_2[2]), .in_2(in_1), .out_3(n8_by_1_bit_multiplier_3_out_3));
  _8_by_1_bit_Multiplier u_8_by_1_bit_multiplier_4 (
    .in_1(in_2[3]), .in_2(in_1), .out_3(n8_by_1_bit_multiplier_4_out_3));
  _8_by_1_bit_Multiplier u_8_by_1_bit_multiplier_5 (
    .in_1(in_2[4]), .in_2(in_1), .out_3(n8_by_1_bit_multiplier_5_out_3));
  _8_by_1_bit_Multiplier u_8_by_1_bit_multiplier_6 (
    .in_1(in_2[5]), .in_2(in_1), .out_3(n8_by_1_bit_multiplier_6_out_3));
  _8_by_1_bit_Multiplier u_8_by_1_bit_multiplier_7 (
    .in_1(in_2[6]), .in_2(in_1), .out_3(n8_by_1_bit_multiplier_7_out_3));
  _8_by_1_bit_Multiplier u_8_by_1_bit_multiplier_8 (
    .in_1(in_2[7]), .in_2(in_1), .out_3(n8_by_1_bit_multiplier_8_out_3));
  _8_Bit_Adder u_8_bit_adder_1 (
    .in_1(1'b0), .in_2(n8_by_1_bit_multiplier_1_out_3), .in_3(n8_by_1_bit_multiplier_2_out_3),
    .out_4(n8_bit_adder_1_out_4));  // open: out_5
  _8_Bit_Adder u_8_bit_adder_2 (
    .in_1(1'b0), .in_2(n8_bit_adder_1_out_4), .out_4(n8_bit_adder_2_out_4));  // open: in_3, out_5
  _8_Bit_Adder u_8_bit_adder_3 (
    .in_1(1'b0), .in_2(n8_bit_adder_2_out_4), .in_3(n8_by_1_bit_multiplier_3_out_3),
    .out_4(n8_bit_adder_3_out_4));  // open: out_5
  _8_Bit_Adder u_8_bit_adder_4 (
    .in_1(1'b0), .in_2(n8_bit_adder_3_out_4), .in_3(n8_by_1_bit_multiplier_4_out_3),
    .out_4(n8_bit_adder_4_out_4));  // open: out_5
  _8_Bit_Adder u_8_bit_adder_5 (
    .in_1(1'b0), .in_2(n8_bit_adder_4_out_4), .in_3(n8_by_1_bit_multiplier_5_out_3),
    .out_4(n8_bit_adder_5_out_4));  // open: out_5
  _8_Bit_Adder u_8_bit_adder_6 (
    .in_1(1'b0), .in_2(n8_bit_adder_5_out_4), .in_3(n8_by_1_bit_multiplier_6_out_3),
    .out_4(n8_bit_adder_6_out_4));  // open: out_5
  _8_Bit_Adder u_8_bit_adder_7 (
    .in_1(1'b0), .in_2(n8_bit_adder_8_out_4), .in_3(n8_by_1_bit_multiplier_8_out_3), .out_4(out_3));  // open: out_5
  _8_Bit_Adder u_8_bit_adder_8 (
    .in_1(1'b0), .in_2(n8_bit_adder_6_out_4), .in_3(n8_by_1_bit_multiplier_7_out_3),
    .out_4(n8_bit_adder_8_out_4));  // open: out_5
endmodule
